// Logisim project seq_circuit.circ as structural Verilog: 1 circuit, main circuit main
module main (
  input  x,
  input  y
);

  wire adder_1_cout, d_ff_1_q, undriven_3;
  wire [7:0] adder_1_out;
  wire [7:1] undriven, undriven_2;

  Adder adder_1 (.a({undriven, x}), .b({undriven_2, y}), .out(adder_1_out), .cin(d_ff_1_q), .cout(adder_1_cout));
  D_Flip_Flop d_ff_1 (.clk(undriven_3), .D(adder_1_cout), .Q(d_ff_1_q));  // open: Qn, preset, reset
  // Pins of 1 and 8 bits meet at {undriven, x}
  // Pins of 1 and 8 bits meet at {undriven_2, y}

  // Notes on the sheet:
  //   Clock
  //   C
  //   S
endmodule
